# Fritzing sketch basic-bot (saved by Fritzing 0.8.3b)
circuit board: 16.9333cm x 5.64444cm
breadboards: 1

parts:
  Arduino1 = Arduino
  M1 = DC Motor
  M2 = DC Motor
  IC1 = L293D [package=THT]
  VCC1 = Battery block 9V

nets:
  N1: Arduino1.GND, IC1.0V, VCC1.-
  N2: Arduino1.D13, IC1.In_3
  N3: Arduino1.D12, IC1.In_4
  N4: Arduino1.D11, IC1.Enable_2
  N5: Arduino1.D10, IC1.Enable_1
  N6: Arduino1.D9, IC1.In_1
  N7: Arduino1.D8, IC1.In_2
  N8: Arduino1.+5V, IC1.+V
  N9: Arduino1.VIN, IC1.+Vmotor, VCC1.+
  N10: M1.pin_1, IC1.Out_4_(_Controlled_by_Enable_2_)
  N11: M1.pin_2, IC1.Out_3_(_Controlled_by_Enable_2_)
  N12: M2.pin_1, IC1.Out_2_(_Controlled_by_Enable_1_)
  N13: M2.pin_2, IC1.Out_1_(_Controlled_by_Enable_1_)
